// Logisim project CC4N-CPU.circ as structural Verilog: 5 circuits, main circuit main
module main (
  input  [3:0] A,
  input  [3:0] B,
  output Overflow,
  output Overflow_2,
  output [3:0] out_5,
  output [3:0] out_6
);

  // Probe on A
  ADD_4 add_4_1 (.in_2(B), .out_3(Overflow), .in_1(A), .out_4(out_5));
  // Probe on out_5
  // Probe on B
  // Probe on A
  Sub_4 sub_4_1 (.A(A), .Overflow(Overflow_2), .B(B), .S(out_6));
  // Probe on out_6
  // Probe on B
endmodule

module ADD_1 (
  input  A,
  input  B,
  input  C,
  output S,
  output Vai_1
);

  wire and_1_out, and_2_out, or_1_out, xor_1_out;

  xor xor_1 (xor_1_out, B, C);
  or or_1 (or_1_out, B, C);
  and and_1 (and_1_out, B, C);
  xor xor_2 (S, xor_1_out, A);
  and and_2 (and_2_out, or_1_out, A);
  or or_2 (Vai_1, and_2_out, and_1_out);
endmodule

module ADD_4 (
  input  [3:0] in_1,
  input  [3:0] in_2,
  output out_3,
  output [3:0] out_4
);

  wire add_1_2_vai_1, add_1_3_vai_1, add_1_4_vai_1;

  // Probe on in_2
  ADD_1 add_1_1 (.Vai_1(out_3), .A(in_2[3]), .B(in_1[3]), .C(add_1_2_vai_1), .S(out_4[3]));
  ADD_1 add_1_2 (.Vai_1(add_1_2_vai_1), .A(in_2[2]), .B(in_1[2]), .C(add_1_3_vai_1), .S(out_4[2]));
  // Probe on out_4
  // Probe on in_1
  ADD_1 add_1_3 (.Vai_1(add_1_3_vai_1), .A(in_2[1]), .B(in_1[1]), .C(add_1_4_vai_1), .S(out_4[1]));
  ADD_1 add_1_4 (.Vai_1(add_1_4_vai_1), .A(in_2[0]), .B(in_1[0]), .C(1'b0), .S(out_4[0]));
endmodule

module Sub_1 (
  input  A,
  input  B,
  input  C,
  output S,
  output Vai_1
);

  wire and_1_out, and_2_out, not_1_out, or_1_out, xor_1_out;

  xor xor_1 (xor_1_out, B, C);
  or or_1 (or_1_out, B, C);
  not not_1 (not_1_out, A);
  and and_1 (and_1_out, B, C);
  xor xor_2 (S, xor_1_out, A);
  and and_2 (and_2_out, or_1_out, not_1_out);
  or or_2 (Vai_1, and_2_out, and_1_out);
endmodule

module Sub_4 (
  input  [3:0] B,
  input  [3:0] A,
  output Overflow,
  output [3:0] S
);

  wire sub_1_2_vai_1, sub_1_3_vai_1, sub_1_4_vai_1;

  // Probe on A
  Sub_1 sub_1_1 (.Vai_1(Overflow), .A(A[3]), .B(B[3]), .C(sub_1_2_vai_1), .S(S[3]));
  Sub_1 sub_1_2 (.Vai_1(sub_1_2_vai_1), .A(A[2]), .B(B[2]), .C(sub_1_3_vai_1), .S(S[2]));
  Sub_1 sub_1_3 (.Vai_1(sub_1_3_vai_1), .A(A[1]), .B(B[1]), .C(sub_1_4_vai_1), .S(S[1]));
  // Probe on S
  Sub_1 sub_1_4 (.Vai_1(sub_1_4_vai_1), .A(A[0]), .B(B[0]), .C(1'b0), .S(S[0]));
  // Probe on B
endmodule
